# Fritzing sketch mmrc-2turnout (saved by Fritzing 0.9.3b)
circuit board: 3.5cm x 1.7cm

parts:
  R3 = Resistor [tolerance=±5% resistance=10k package=THT]
  R2 = Resistor [tolerance=±5% resistance=680 package=THT]
  R1 = Resistor [tolerance=±5% resistance=680 package=THT]
  J5 = male pin header, 3 pins [form="♂ (male)"]
  J4 = male pin header, 4 pins [form="♂ (male)"]
  J2 = female pin header, 3 pins [form="♀ (female)"]
  J9 = male pin header, 3 pins [form="♂ (male)"]
  J1 = male pin header, 5 pins [form="♂ (male)"]
  J3 = female pin header, 3 pins [form="♀ (female)"]

nets:
  N1: R3.Pin_0, J4.pin3, J1.pin3
  N2: R3.Pin_1, J2.pin3, J3.pin3
  N3: R2.Pin_0, J1.pin2
  N4: R2.Pin_1, J4.pin2
  N5: R1.Pin_0, J1.pin1
  N6: R1.Pin_1, J4.pin1
  N7: J5.pin1, J4.pin4, J2.pin1, J9.pin1, J3.pin1
  N8: J5.pin2, J2.pin2, J9.pin2, J3.pin2
  N9: J5.pin3, J1.pin4
  N10: J9.pin3, J1.pin5

notes:
  Servo
  -
  Btn
  L2
  L1
  191226
  5V
  LED1
  LED2
  D5
  D6
  D7
  D8
  +
  Wemos
  LED
  Knapp
  Arduino
  GND
  3V
  DC-anslutning
  DC in/out
  S2
  S1
